# Fritzing sketch petmouse (saved by Fritzing 0.9.0b)
breadboards: 1

parts:
  Componente1 = Arduino Uno (Rev3)
  pan_servo = Basic Servo
  4_7_kiloohm = Resistor [tolerance=±5% resistance=4.7k package="1206 [SMD]"]
  4_7_kiloohm2 = Resistor [tolerance=±5% resistance=4.7k package="1206 [SMD]"]
  1_kiloohm = Resistor [tolerance=±5% resistance=1k package="1206 [SMD]"]
  1_kiloohm1 = Resistor [tolerance=±5% resistance=1k package="1206 [SMD]"]
  2_2_kiloohm = Resistor [tolerance=±5% resistance=2.2k package="1206 [SMD]"]
  2_2_kiloohm1 = Resistor [tolerance=±5% resistance=2.2k package="1206 [SMD]"]
  47_ohm = Resistor [tolerance=±5% resistance=47 package="1206 [SMD]"]
  47_ohm1 = Resistor [tolerance=±5% resistance=47 package="1206 [SMD]"]
  4_7_microfarad = Ceramic Capacitor [capacitance=4.7µF package="0603 [SMD, multilayer]"]
  4_7_microfarad1 = Ceramic Capacitor [capacitance=4.7µF package="0603 [SMD, multilayer]"]
  U1 = TRANSCHIPTC5747 [package=camera_sfv24r-2st_2]  # not connected
  tilt_servo = Basic Servo
  BeagleBone1 = BeagleBone Black
  JACK6 = 2.1mm DC Barrel Jack  # not connected
  JACK8 = 2.1mm DC Barrel Jack  # not connected
  JACK10 = 2.1mm DC Barrel Jack  # not connected
  JACK11 = 2.1mm DC Barrel Jack  # not connected
  JACK12 = 2.1mm DC Barrel Jack  # not connected
  JACK13 = 2.1mm DC Barrel Jack  # not connected
  JACK14 = 2.1mm DC Barrel Jack  # not connected
  JACK15 = 2.1mm DC Barrel Jack  # not connected
  JACK16 = 2.1mm DC Barrel Jack  # not connected

nets:
  N1: Componente1.GND, 2_2_kiloohm.Pin_0, 2_2_kiloohm1.Pin_0, 4_7_microfarad.0, 4_7_microfarad1.0, BeagleBone1.no_name_yet#32, BeagleBone1.no_name_yet#34
  N2: Componente1.D5_PWM, 4_7_kiloohm.Pin_0
  N3: Componente1.D6_PWM, 4_7_kiloohm2.Pin_0
  N4: pan_servo.vcc, BeagleBone1.no_name_yet#3, BeagleBone1.no_name_yet#5, BeagleBone1.no_name_yet#7
  N5: pan_servo.pulse, 1_kiloohm1.Pin_0
  N6: 4_7_kiloohm.Pin_1, 2_2_kiloohm.Pin_1, 47_ohm1.Pin_0, 4_7_microfarad.1
  N7: 4_7_kiloohm2.Pin_1, 2_2_kiloohm1.Pin_1, 47_ohm.Pin_0, 4_7_microfarad1.1
  N8: 1_kiloohm.Pin_0, tilt_servo.pulse
  N9: 1_kiloohm.Pin_1, BeagleBone1.no_name_yet#20, BeagleBone1.no_name_yet#22
  N10: 1_kiloohm1.Pin_1, BeagleBone1.no_name_yet#12, BeagleBone1.no_name_yet#14
  N11: 47_ohm.Pin_1, 47_ohm1.Pin_1, BeagleBone1.no_name_yet#31, BeagleBone1.no_name_yet#33
  N12: tilt_servo.vcc, BeagleBone1.no_name_yet#4, BeagleBone1.no_name_yet#6, BeagleBone1.no_name_yet#8

notes:
  Pixy CMUCam5
  Tilt servo
  Pan servo
  4.7 μF
  1 kΩ
  47 Ω
  2.2 kΩ
  4.7 kΩ
  5 V 1 A supply
  Low-pass filter for PWM x signal: green wire, 4.7 kΩ resistor, 4.7 μF capacitor
  Low-pass filter for PWM y signal: white wire, 4.7 kΩ resistor, 4.7 μF capacitor
  Voltage divider for analog x signal: green wire, 2.2 kΩ and 47 Ω resistors
  Voltage divider for analog y signal: white wire, 2.2 kΩ and 47 Ω resistors
  Resistors for micro servo motors: 1 kΩ

custom parts:
  BeagleBone Black: BeagleBone Black rev. A5B
  2.1mm DC Barrel Jack: 2.1mm DC Barrel Jack with Thru-Hole Connectors (breadboardable)
